// Logisim project rs-trigger.circ as structural Verilog: 1 circuit, main circuit main
module main (
  input  S,
  input  C,
  input  R,
  output nQ,
  output Q
);

  wire and_1_out, and_2_out, or_1_out, or_2_out;

  and and_1 (and_1_out, S, C);
  and and_2 (and_2_out, C, R);
  or or_1 (or_1_out, and_1_out, Q);
  not not_1 (nQ, or_1_out);
  or or_2 (or_2_out, nQ, and_2_out);
  not not_2 (Q, or_2_out);
endmodule
