// Logisim project adder.circ as structural Verilog: 2 circuits, main circuit ODS_3_PCNF
module ODS_3_PCNF (
  input  in_1,
  input  in_2,
  input  in_3,
  output Sum,
  output Carry_Out
);

  wire not_1_out, not_2_out, not_3_out, or_1_out, or_2_out, or_3_out, or_4_out, or_5_out, or_6_out, or_7_out;

  not not_1 (not_1_out, in_1);
  not not_2 (not_2_out, in_2);
  not not_3 (not_3_out, in_3);
  or or_1 (or_1_out, in_1, in_2, in_3);
  or or_2 (or_2_out, in_1, not_2_out, not_3_out);
  or or_3 (or_3_out, not_1_out, in_2, not_3_out);
  or or_4 (or_4_out, not_1_out, not_2_out, in_3);
  or or_5 (or_5_out, in_2, in_3);
  or or_6 (or_6_out, in_1, in_3);
  or or_7 (or_7_out, in_1, in_2);
  and and_1 (Sum, or_1_out, or_2_out, or_3_out, or_4_out);
  and and_2 (Carry_Out, or_5_out, or_6_out, or_7_out);

  // Notes on the sheet:
  //   C
  //   B
  //   A
  //   !B
  //   !C
  //   !A
endmodule

module _8_BIT_ADDER (
  input  [7:0] A,
  input  [7:0] B,
  output [7:0] C
);

  wire ods_3_pcnf_1_carry_out, ods_3_pcnf_2_carry_out, ods_3_pcnf_3_carry_out, ods_3_pcnf_4_carry_out,
       ods_3_pcnf_5_carry_out, ods_3_pcnf_6_carry_out, ods_3_pcnf_7_carry_out;

  // Probe on C
  // Probe on A
  // Probe on B
  ODS_3_PCNF ods_3_pcnf_1 (.in_1(A[0]), .in_2(B[0]), .in_3(1'b0), .Sum(C[0]), .Carry_Out(ods_3_pcnf_1_carry_out));
  ODS_3_PCNF ods_3_pcnf_2 (
    .in_1(A[1]), .in_2(B[1]), .in_3(ods_3_pcnf_1_carry_out), .Sum(C[1]), .Carry_Out(ods_3_pcnf_2_carry_out));
  ODS_3_PCNF ods_3_pcnf_3 (
    .in_1(A[2]), .in_2(B[2]), .in_3(ods_3_pcnf_2_carry_out), .Sum(C[2]), .Carry_Out(ods_3_pcnf_3_carry_out));
  ODS_3_PCNF ods_3_pcnf_4 (
    .in_1(A[3]), .in_2(B[3]), .in_3(ods_3_pcnf_3_carry_out), .Sum(C[3]), .Carry_Out(ods_3_pcnf_4_carry_out));
  ODS_3_PCNF ods_3_pcnf_5 (
    .in_1(A[4]), .in_2(B[4]), .in_3(ods_3_pcnf_4_carry_out), .Sum(C[4]), .Carry_Out(ods_3_pcnf_5_carry_out));
  ODS_3_PCNF ods_3_pcnf_6 (
    .in_1(A[5]), .in_2(B[5]), .in_3(ods_3_pcnf_5_carry_out), .Sum(C[5]), .Carry_Out(ods_3_pcnf_6_carry_out));
  ODS_3_PCNF ods_3_pcnf_7 (
    .in_1(A[6]), .in_2(B[6]), .in_3(ods_3_pcnf_6_carry_out), .Sum(C[6]), .Carry_Out(ods_3_pcnf_7_carry_out));
  ODS_3_PCNF ods_3_pcnf_8 (.in_1(A[7]), .in_2(B[7]), .in_3(ods_3_pcnf_7_carry_out), .Sum(C[7]));  // open: Carry_Out
endmodule
