// Logisim project d8421_9.circ as structural Verilog: 1 circuit, main circuit main
module main (
  input  [3:0] D,
  output [3:0] out_2
);

  wire not_1_out, not_2_out, not_3_out, not_4_out, or_1_out, or_2_out, or_3_out, or_4_out, or_5_out,
       or_6_out, or_7_out, or_8_out, or_9_out, or_10_out, or_11_out, or_12_out, or_13_out;

  // Probe on D
  not not_1 (not_1_out, D[0]);
  not not_2 (not_2_out, D[3]);
  not not_3 (not_3_out, D[1]);
  not not_4 (not_4_out, D[2]);
  or or_1 (or_1_out, D[3], not_1_out);
  or or_2 (or_2_out, D[0], not_2_out);
  or or_3 (or_3_out, not_1_out, D[2]);
  or or_4 (or_4_out, not_2_out, not_4_out);
  or or_5 (or_5_out, D[2], not_3_out);
  or or_6 (or_6_out, D[3], D[1], D[0]);
  or or_7 (or_7_out, D[1], not_1_out);
  or or_8 (or_8_out, not_3_out, D[0]);
  or or_9 (or_9_out, not_2_out, not_1_out);
  or or_10 (or_10_out, D[3], D[2], D[0]);
  or or_11 (or_11_out, not_2_out, not_4_out);
  or or_12 (or_12_out, not_2_out, not_3_out);
  or or_13 (or_13_out, not_2_out, not_4_out);
  and A (out_2[3], or_1_out, not_4_out, not_3_out, or_2_out);
  and B (out_2[2], or_3_out, or_4_out, or_5_out, or_6_out);
  and C (out_2[1], or_7_out, or_8_out, or_9_out, or_10_out, or_11_out);
  and u_D (out_2[0], or_12_out, not_1_out, or_13_out);
  // Probe on out_2

  // Notes on the sheet:
  //   D
  //   C
  //   B
  //   A
  //   !D
  //   !C
  //   !B
  //   !A
endmodule
